// Logisim project piplineRegisters.circ as structural Verilog
module main (
);

  IF_ID IF_ID ();  // open: PC_in, Instruc_in, clk, PC_out, Instruc_out
endmodule

module IF_ID (
  input  [7:0] PC_in,
  input  [15:0] Instruc_in,
  input  clk,
  output [7:0] PC_out,
  output [15:0] Instruc_out
);

  Register PC (.D(PC_in), .Q(PC_out), .clk(clk));  // open: en, clr
  Register #(.width(16)) Instruction (.D(Instruc_in), .Q(Instruc_out), .clk(clk));  // open: en, clr
endmodule
